# Fritzing sketch buzzer (saved by Fritzing 0.9.3b)
breadboards: 1

parts:
  Part1 = Arduino Ethernet Shield (Rev3)
  S1 = Pushbutton [package="[THT]"]
  J1 = Piezo Speaker

nets:
  N1: Part1.PWM_D3, S1.Pin_1, S1.Pin_2
  N2: Part1.D7, J1.pin1
  N3: Part1.5V, S1.Pin_3, S1.Pin_4
  N4: Part1.GND, J1.pin2
