# Fritzing sketch dht (saved by Fritzing 0.9.3b)

parts:
  RHT1 = Humidity and Temperature Sensor RHT03
  Part1 = Arduino Ethernet Shield (Rev3)

nets:
  VCC: RHT1.Vcc, Part1.5V
  N1: RHT1.Data-signal, Part1.PWM_D9
  N2: RHT1.GND_2, Part1.GND
