# Fritzing sketch Infrared_Sensor (saved by Fritzing 0.9.3b)
breadboards: 1

parts:
  J1 = Infrared Proximity Sensor
  Arduino1 = Arduino Uno (Rev3)

nets:
  N1: J1.Vout, Arduino1.D7
  GND: J1.GND, Arduino1.GND
  VCC: J1.Vcc, Arduino1.5V
