# Fritzing sketch multiplelight (saved by Fritzing 0.9.3b)
breadboards: 1

parts:
  Part1 = Arduino Ethernet Shield (Rev3)
  LED1 = LED - 5mm [color="Red (633nm)" package="5 mm [THT]"]
  LED2 = LED - 5mm [color="Red (633nm)" package="5 mm [THT]"]
  LED3 = LED - 5mm [color="Red (633nm)" package="5 mm [THT]"]

nets:
  N1: Part1.GND, LED1.anode, LED2.anode, LED3.anode
  N2: Part1.D2, LED3.cathode
  N3: Part1.SDCS, LED2.cathode
  N4: Part1.PWM_D5, LED1.cathode
