# Fritzing sketch pir (saved by Fritzing 0.9.3b)
breadboards: 1

parts:
  Sensore_PIR_HC-SR501 = HC-SR501 Body Sensor Module
  Part1 = Arduino Ethernet Shield (Rev3)
  LED1 = LED - 5mm [color="Red (633nm)" package="5 mm [THT]"]

nets:
  VCC: Sensore_PIR_HC-SR501.VCC, Part1.3V3
  N1: Sensore_PIR_HC-SR501.OUT, Part1.ETH_CS
  GND: Sensore_PIR_HC-SR501.GND, Part1.GND, LED1.anode
  N2: Part1.PWM_D5, LED1.cathode

custom parts:
  HC-SR501 Body Sensor Module: Pyroelectric Infrared PIR Motion Sensor Detector Module
