# Fritzing sketch pressure (saved by Fritzing 0.9.3b)

parts:
  Part1 = Barometric Pressure Sensor - BMP180 Breakout (GY-68)
  Part2 = Arduino Ethernet Shield (Rev3)

nets:
  VCC: Part1.VCC, Part2.3V3
  GND: Part1.GND, Part2.GND
  N1: Part1.SCL, Part2.A5/SCL
  N2: Part1.SDA, Part2.A4/SDA
