# Fritzing sketch sonic (saved by Fritzing 0.9.3b)

parts:
  Part2 = SRF05 Ultrasonic Rangefinder
  Part4 = Arduino Ethernet Shield (Rev3)

nets:
  VCC: Part2.VCC, Part4.5V
  N1: Part2.Trig, Part4.D7
  N2: Part2.Echo, Part4.D8
  GND: Part2.GND, Part4.GND
